# Fritzing sketch Elektrisch Design (saved by Fritzing 0.9.3b)
breadboards: 1

parts:
  Master_Arduino = Arduino Uno (Rev3) - ICSP
  RFID_Arduino = Arduino Uno (Rev3) - ICSP
  Keypad_Arduino = Arduino Uno (Rev3) - ICSP
  Printer_Arduino = Arduino Uno (Rev3) - ICSP
  Keypad_4x4 = Keypad Membran 4x4
  RFID_Scanner = RFID-RC522-v2
  Printer = Thermal Printer
  Aansluiting_stopcontact = DC Power [voltage=5V]

nets:
  N1: Master_Arduino.A4/SDA, RFID_Arduino.ICSP_MISO
  N2: Master_Arduino.A5/SCL, RFID_Arduino.A5/SCL, Keypad_Arduino.A5/SCL, Printer_Arduino.A5/SCL
  VIN: Master_Arduino.5V, RFID_Arduino.VIN, Keypad_Arduino.VIN
  GND: Master_Arduino.GND, RFID_Arduino.GND, Keypad_Arduino.GND, Printer_Arduino.GND, RFID_Scanner.RST, Printer.GND#0, Aansluiting_stopcontact.V-
  N3: RFID_Arduino.A4/SDA, Keypad_Arduino.A4/SDA
  N4: RFID_Arduino.D10_PWM/SS, RFID_Scanner.SDA
  N5: RFID_Arduino.D11_PWM/MOSI, RFID_Scanner.MOSI
  N6: RFID_Arduino.D12/MISO, RFID_Scanner.MISO
  N7: RFID_Arduino.D13/SCK, RFID_Scanner.SCK
  N8: RFID_Arduino.D5_PWM, RFID_Scanner.GND
  3V3: RFID_Arduino.3V3, RFID_Scanner.3.3V
  N9: Keypad_Arduino.ICSP_MISO, Printer_Arduino.A4/SDA
  N10: Keypad_Arduino.D8, Keypad_4x4.Pin2
  N11: Keypad_Arduino.D9_PWM, Keypad_4x4.Pin1
  N12: Keypad_Arduino.D2, Keypad_4x4.Pin8
  N13: Keypad_Arduino.D3_PWM, Keypad_4x4.Pin7
  N14: Keypad_Arduino.D4, Keypad_4x4.Pin6
  N15: Keypad_Arduino.D5_PWM, Keypad_4x4.Pin5
  N16: Keypad_Arduino.D6_PWM, Keypad_4x4.Pin4
  N17: Keypad_Arduino.D7, Keypad_4x4.Pin3
  N18: Printer_Arduino.D5_PWM, Printer.RXD
  N19: Printer_Arduino.D6_PWM, Printer.TXD
  N20: Printer_Arduino.VIN, Printer.VH, Aansluiting_stopcontact.V+

custom parts:
  Keypad Membran 4x4: Membrane Keypad 4x4 Matrix
  RFID-RC522-v2: A simple China made RFID-RC522 Reader; do check the pin labels, as this is a MFRC522 based clone.
